# Fritzing sketch Sani-oz (saved by Fritzing 0.9.3b)

parts:
  R2 = Resistor [tolerance=±5% resistance=220 package=THT]  # not connected
  D2 = Rectifier Diode [part_number=1N4001 package="300 mil [THT]"]  # not connected
  t1 = Transformador
  J3 = valvula
  R3 = Resistor [tolerance=±5% resistance=220 package=THT]  # not connected
  D3 = Rectifier Diode [part_number=1N4001 package="300 mil [THT]"]  # not connected
  Q3 = Basic FET P-Channel [package="TO220 [THT]"]
  t2 = Transformador
  J10 = placa [form="♀ (female)"]
  J11 = Generic female header - 1 pins [form="♀ (female)"]
  J12 = sensor de OXIGENO [form="♀ (female)"]
  Q2 = Basic FET P-Channel [package="TO220 [THT]"]
  Componente2 = Arduino Ethernet Shield (Rev3)
  F1 = Fan - Ventilador [package=THT]
  Componente3 = Arduino Ethernet Shield (Rev3)

nets:
  N1: t1.pin3, t1.pin4
  N2: t1.pin6, J3.pin1
  N3: Q3.source, Componente3.GND
  N4: t2.pin3, t2.pin4
  N5: t2.pin5, J10.pin1
  N6: t2.pin6, J11.pin1
  GND: J12.pin1, Q2.source, Componente2.GND, F1.GND
  5V: J12.pin2, Componente2.5V, F1.5V
  N7: J12.pin4, Componente2.A0

notes:
  IONIZADOR
  GENERADOR DE OZONO

custom parts:
  valvula: Generic female header
  Generic female header - 1 pins: Generic female header
  sensor de OXIGENO: SENSOR DE OXIGENO
  Fan - Ventilador: Ventilador de 2 pines, se encuentra comunmente en computadoras de escritorio
